// Logisim project ALU1BYTE.circ as structural Verilog: 1 circuit, main circuit main
module main (
  input  in_1,
  input  in_2,
  input  in_3,
  input  in_4,
  input  in_5,
  input  in_6,
  input  in_7,
  input  in_8,
  input  in_9,
  input  in_10,
  input  in_11,
  input  in_12,
  input  in_13,
  input  in_14,
  input  in_15,
  input  in_16,
  input  in_17,
  input  in_18,
  input  in_19,
  input  in_20,
  input  in_21,
  input  in_22,
  input  in_23,
  input  in_24,
  input  in_25,
  input  in_26,
  input  in_27,
  input  in_28,
  input  in_29,
  input  in_30,
  input  in_31,
  input  in_32,
  input  in_33,
  input  in_34,
  input  in_35,
  input  in_36,
  input  INPUT__B,
  input  in_38,
  input  in_39,
  input  in_40,
  input  in_41,
  input  [3:0] in_42,
  input  OPCODES,
  input  ADD__0001,
  input  SUB__0010,
  input  in_46,
  input  OR__0011,
  input  AND__0100,
  input  in_49,
  input  XOR__0101,
  input  NOT__0110,
  input  NOR__0111,
  input  NAND__1000,
  input  XNOR__1001,
  input  in_55,
  input  in_56,
  input  in_57,
  input  in_58,
  input  in_59,
  input  in_60,
  input  in_61,
  input  in_62,
  input  in_63,
  input  USER_INPUT,
  input  in_65,
  input  in_66,
  input  in_67,
  input  in_68,
  input  in_69,
  input  in_70
);

  wire and_1_out, and_2_out, and_3_out, and_4_out, and_5_out, and_6_out, and_7_out, and_8_out, and_9_out,
       and_10_out, and_11_out, and_12_out, and_13_out, and_14_out, and_15_out, and_16_out, and_17_out,
       and_18_out, and_19_out, and_20_out, and_21_out, and_22_out, and_23_out, and_24_out, and_25_out,
       and_26_out, and_27_out, and_28_out, and_29_out, and_30_out, and_31_out, and_32_out, and_33_out,
       and_34_out, and_35_out, and_36_out, and_37_out, and_38_out, and_39_out, and_40_out, and_41_out,
       and_42_out, and_43_out, and_44_out, and_45_out, and_46_out, and_47_out, and_48_out, and_49_out,
       and_50_out, and_51_out, and_52_out, and_53_out, and_54_out, and_55_out, and_56_out, and_57_out,
       and_58_out, and_59_out, and_60_out, and_61_out, and_62_out, and_63_out, and_64_out, and_65_out,
       and_66_out, and_67_out, and_68_out, and_69_out, and_70_out, and_71_out, and_72_out, and_73_out,
       and_74_out, and_75_out, and_76_out, and_77_out, and_78_out, and_79_out, and_80_out, and_81_out,
       and_82_out, and_83_out, and_84_out, and_85_out, and_86_out, and_87_out, and_88_out, and_89_out,
       and_90_out, and_91_out, and_92_out, and_93_out, and_94_out, and_95_out, and_96_out,
       bcd_to_7_segment_decoder_1_p1, bcd_to_7_segment_decoder_1_p2, bcd_to_7_segment_decoder_1_p3,
       bcd_to_7_segment_decoder_1_p4, bcd_to_7_segment_decoder_1_p6, bcd_to_7_segment_decoder_1_p7,
       bcd_to_7_segment_decoder_1_p8, bcd_to_7_segment_decoder_2_p1, bcd_to_7_segment_decoder_2_p2,
       bcd_to_7_segment_decoder_2_p3, bcd_to_7_segment_decoder_2_p4, bcd_to_7_segment_decoder_2_p6,
       bcd_to_7_segment_decoder_2_p7, bcd_to_7_segment_decoder_2_p8, bcd_to_7_segment_decoder_3_p1,
       bcd_to_7_segment_decoder_3_p2, bcd_to_7_segment_decoder_3_p3, bcd_to_7_segment_decoder_3_p4,
       bcd_to_7_segment_decoder_3_p6, bcd_to_7_segment_decoder_3_p7, bcd_to_7_segment_decoder_3_p8,
       bcd_to_7_segment_decoder_4_p1, bcd_to_7_segment_decoder_4_p2, bcd_to_7_segment_decoder_4_p3,
       bcd_to_7_segment_decoder_4_p4, bcd_to_7_segment_decoder_4_p6, bcd_to_7_segment_decoder_4_p7,
       bcd_to_7_segment_decoder_4_p8, bcd_to_7_segment_decoder_5_p1, bcd_to_7_segment_decoder_5_p2,
       bcd_to_7_segment_decoder_5_p3, bcd_to_7_segment_decoder_5_p4, bcd_to_7_segment_decoder_5_p6,
       bcd_to_7_segment_decoder_5_p7, bcd_to_7_segment_decoder_5_p8, bcd_to_7_segment_decoder_6_p1,
       bcd_to_7_segment_decoder_6_p2, bcd_to_7_segment_decoder_6_p3, bcd_to_7_segment_decoder_6_p4,
       bcd_to_7_segment_decoder_6_p6, bcd_to_7_segment_decoder_6_p7, bcd_to_7_segment_decoder_6_p8,
       bcd_to_7_segment_decoder_7_p1, bcd_to_7_segment_decoder_7_p2, bcd_to_7_segment_decoder_7_p3,
       bcd_to_7_segment_decoder_7_p4, bcd_to_7_segment_decoder_7_p6, bcd_to_7_segment_decoder_7_p7,
       bcd_to_7_segment_decoder_7_p8, bcd_to_7_segment_decoder_8_p1, bcd_to_7_segment_decoder_8_p2,
       bcd_to_7_segment_decoder_8_p3, bcd_to_7_segment_decoder_8_p4, bcd_to_7_segment_decoder_8_p6,
       bcd_to_7_segment_decoder_8_p7, bcd_to_7_segment_decoder_8_p8, bcd_to_7_segment_decoder_9_p1,
       bcd_to_7_segment_decoder_9_p2, bcd_to_7_segment_decoder_9_p3, bcd_to_7_segment_decoder_9_p4,
       bcd_to_7_segment_decoder_9_p6, bcd_to_7_segment_decoder_9_p7, bcd_to_7_segment_decoder_9_p8,
       bcd_to_7_segment_decoder_10_p1, bcd_to_7_segment_decoder_10_p2, bcd_to_7_segment_decoder_10_p3,
       bcd_to_7_segment_decoder_10_p4, bcd_to_7_segment_decoder_10_p6, bcd_to_7_segment_decoder_10_p7,
       bcd_to_7_segment_decoder_10_p8, bcd_to_7_segment_decoder_11_p1, bcd_to_7_segment_decoder_11_p2,
       bcd_to_7_segment_decoder_11_p3, bcd_to_7_segment_decoder_11_p4, bcd_to_7_segment_decoder_11_p6,
       bcd_to_7_segment_decoder_11_p7, bcd_to_7_segment_decoder_11_p8, bcd_to_7_segment_decoder_12_p1,
       bcd_to_7_segment_decoder_12_p2, bcd_to_7_segment_decoder_12_p3, bcd_to_7_segment_decoder_12_p4,
       bcd_to_7_segment_decoder_12_p6, bcd_to_7_segment_decoder_12_p7, bcd_to_7_segment_decoder_12_p8,
       binary_to_bcd_converter_1_p2, binary_to_bcd_converter_1_p3, binary_to_bcd_converter_1_p4,
       binary_to_bcd_converter_2_p2, binary_to_bcd_converter_2_p3, binary_to_bcd_converter_2_p4,
       binary_to_bcd_converter_3_p2, binary_to_bcd_converter_3_p3, binary_to_bcd_converter_3_p4,
       binary_to_bcd_converter_4_p2, binary_to_bcd_converter_4_p3, binary_to_bcd_converter_4_p4,
       decoder_1_out1, decoder_1_out2, decoder_1_out3, decoder_1_out4, decoder_1_out5, decoder_1_out6,
       decoder_1_out7, decoder_1_out8, decoder_1_out9, decoder_1_out10, decoder_1_out11, decoder_1_out12,
       decoder_1_out13, decoder_1_out14, decoder_2_out1, decoder_2_out2, decoder_2_out3, decoder_2_out4,
       decoder_2_out5, decoder_2_out6, decoder_2_out7, decoder_2_out8, decoder_2_out9, decoder_2_out10,
       decoder_2_out11, decoder_2_out12, decoder_2_out13, decoder_2_out14, multiplexer_1_out,
       multiplexer_2_out, multiplexer_3_out, multiplexer_4_out, multiplexer_5_out, multiplexer_6_out,
       multiplexer_7_out, multiplexer_8_out, multiplexer_9_out, multiplexer_10_out, multiplexer_11_out,
       multiplexer_12_out, multiplexer_13_out, multiplexer_14_out, multiplexer_15_out, multiplexer_16_out,
       multiplexer_17_out, multiplexer_18_out, multiplexer_19_out, multiplexer_20_out, multiplexer_21_out,
       multiplexer_22_out, multiplexer_23_out, multiplexer_24_out, multiplexer_25_out, multiplexer_26_out,
       multiplexer_27_out, multiplexer_28_out, multiplexer_29_out, multiplexer_30_out, multiplexer_31_out,
       multiplexer_32_out, multiplexer_33_out, multiplexer_34_out, multiplexer_35_out, multiplexer_36_out,
       multiplexer_38_out, multiplexer_39_out, multiplexer_40_out, multiplexer_42_out, multiplexer_43_out,
       multiplexer_45_out, multiplexer_46_out, multiplexer_47_out, multiplexer_48_out, multiplexer_50_out,
       multiplexer_51_out, multiplexer_53_out, multiplexer_54_out, multiplexer_55_out, multiplexer_57_out,
       multiplexer_58_out, multiplexer_59_out, multiplexer_60_out, multiplexer_62_out, multiplexer_63_out,
       not_1_out, not_2_out, not_3_out, not_4_out, not_5_out, not_6_out, not_7_out, not_8_out, not_9_out,
       not_10_out, not_11_out, not_12_out, not_13_out, not_14_out, not_15_out, not_16_out, not_17_out,
       not_18_out, not_19_out, not_20_out, not_21_out, not_22_out, or_1_out, or_2_out, or_3_out, or_4_out,
       or_5_out, or_6_out, or_7_out, or_8_out, or_9_out, or_10_out, or_11_out, or_12_out, or_13_out,
       or_14_out, or_15_out, or_16_out, or_17_out, or_18_out, or_19_out, or_20_out, or_21_out, or_22_out,
       or_23_out, or_24_out, or_29_out, or_30_out, or_31_out, or_32_out, or_33_out, or_34_out, or_35_out,
       or_36_out, or_37_out, or_38_out, or_39_out, or_40_out, or_41_out, or_42_out, or_43_out, or_44_out,
       or_45_out, or_46_out, or_47_out, or_48_out, or_49_out, or_50_out, or_51_out, or_52_out, xor_1_out,
       xor_2_out, xor_3_out, xor_4_out, xor_5_out, xor_6_out, xor_7_out, xor_8_out, xor_9_out, xor_10_out,
       xor_11_out, xor_12_out, xor_13_out, xor_14_out, xor_15_out, xor_16_out, xor_17_out, xor_18_out,
       xor_19_out, xor_20_out, xor_21_out, xor_22_out, xor_23_out, xor_24_out, xor_25_out, xor_26_out,
       xor_27_out, xor_28_out, xor_29_out, xor_30_out, xor_31_out, xor_32_out, xor_33_out, xor_34_out,
       xor_35_out, xor_36_out, xor_37_out, xor_38_out, xor_39_out, xor_40_out, xor_41_out, xor_42_out,
       xor_43_out, xor_44_out, xor_45_out, xor_46_out, xor_47_out, xor_48_out, xor_49_out, xor_50_out,
       xor_51_out, xor_52_out, xor_53_out, xor_54_out, xor_55_out, xor_56_out, xor_57_out, xor_58_out,
       xor_59_out, xor_60_out, xor_61_out, xor_62_out, xor_63_out, xor_64_out;
  wire [3:0] or_25_out;
  wire [7:0] multiplexer_37_out;

  Decoder #(.select(4)) decoder_1 (
    .out1(decoder_1_out1), .out2(decoder_1_out2), .out3(decoder_1_out3), .out4(decoder_1_out4),
    .out5(decoder_1_out5), .out6(decoder_1_out6), .out7(decoder_1_out7), .out8(decoder_1_out8),
    .out9(decoder_1_out9), .out10(decoder_1_out10), .out11(decoder_1_out11), .out12(decoder_1_out12),
    .out13(decoder_1_out13), .out14(decoder_1_out14), .sel(in_42), .en(in_41));  // open: out0, out15
  or or_1 (or_1_out, decoder_1_out13, decoder_1_out12, decoder_1_out6);
  Multiplexer multiplexer_1 (.in0(in_3), .in1(in_4), .out(multiplexer_1_out), .sel(decoder_1_out14));
  not not_1 (not_1_out, or_1_out);
  and and_1 (and_1_out, in_5, not_1_out);
  or or_2 (or_2_out, decoder_1_out2, decoder_1_out11, decoder_1_out10, decoder_1_out3, decoder_1_out7);
  xor xor_1 (xor_1_out, multiplexer_1_out, or_3_out);
  or or_3 (or_3_out, decoder_1_out3, decoder_1_out7, decoder_1_out6);
  xor xor_2 (xor_2_out, xor_1_out, xor_4_out);
  xor xor_3 (xor_3_out, xor_2_out, decoder_1_out2);
  or or_4 (or_4_out, decoder_1_out1, decoder_1_out2, decoder_1_out6, decoder_1_out12);
  and and_2 (and_2_out, xor_3_out, or_4_out);
  or or_5 (or_5_out, decoder_1_out5, decoder_1_out13, decoder_1_out9, decoder_1_out14);
  or or_6 (or_6_out, decoder_1_out8, decoder_1_out3, decoder_1_out11, decoder_1_out4, decoder_1_out7, decoder_1_out10);
  and and_3 (and_3_out, or_6_out, and_4_out);
  or or_7 (or_7_out, decoder_1_out8, decoder_1_out10, decoder_1_out3, decoder_1_out9);
  not not_2 (not_2_out, decoder_1_out13);
  Multiplexer multiplexer_2 (.in0(in_6), .in1(in_7), .out(multiplexer_2_out), .sel(decoder_1_out14));
  xor xor_4 (xor_4_out, and_1_out, or_2_out);
  xor xor_5 (xor_5_out, multiplexer_2_out, or_3_out);
  and and_4 (and_4_out, xor_4_out, xor_1_out);
  and and_5 (and_5_out, decoder_1_out2, xor_2_out);
  or or_8 (or_8_out, and_5_out, and_4_out);
  and and_6 (and_6_out, xor_2_out, or_5_out);
  or or_9 (or_9_out, and_3_out, and_6_out, and_2_out);
  not not_3 (not_3_out, or_9_out);
  Multiplexer multiplexer_3 (.in0(or_9_out), .in1(not_3_out), .out(multiplexer_3_out), .sel(or_7_out));
  Multiplexer multiplexer_4 (
    .in0(multiplexer_3_out), .in1(multiplexer_6_out), .out(multiplexer_4_out), .sel(decoder_1_out12));
  Multiplexer multiplexer_5 (.in0(in_49), .in1(multiplexer_4_out), .out(multiplexer_5_out), .sel(not_2_out));
  LED led_1 (.in(multiplexer_5_out));
  LED led_2 (.in(multiplexer_8_out));
  and and_7 (and_7_out, in_8, not_1_out);
  xor xor_6 (xor_6_out, and_7_out, or_2_out);
  xor xor_7 (xor_7_out, xor_5_out, xor_6_out);
  and and_8 (and_8_out, xor_6_out, xor_5_out);
  and and_9 (and_9_out, or_8_out, xor_7_out);
  xor xor_8 (xor_8_out, xor_7_out, or_8_out);
  or or_10 (or_10_out, and_9_out, and_8_out);
  and and_10 (and_10_out, xor_8_out, or_4_out);
  and and_11 (and_11_out, xor_7_out, or_5_out);
  and and_12 (and_12_out, or_6_out, and_8_out);
  or or_11 (or_11_out, and_12_out, and_11_out, and_10_out);
  not not_4 (not_4_out, or_11_out);
  Multiplexer multiplexer_6 (.in0(or_11_out), .in1(not_4_out), .out(multiplexer_6_out), .sel(or_7_out));
  Multiplexer multiplexer_7 (
    .in0(multiplexer_6_out), .in1(multiplexer_11_out), .out(multiplexer_7_out), .sel(decoder_1_out12));
  Multiplexer multiplexer_8 (
    .in0(multiplexer_4_out), .in1(multiplexer_7_out), .out(multiplexer_8_out), .sel(not_2_out));
  LED led_3 (.in(multiplexer_13_out));
  LED led_4 (.in(multiplexer_17_out));
  LED led_5 (.in(multiplexer_20_out));
  Multiplexer multiplexer_9 (.in0(in_9), .in1(in_10), .out(multiplexer_9_out), .sel(decoder_1_out14));
  and and_13 (and_13_out, in_11, not_1_out);
  xor xor_9 (xor_9_out, multiplexer_9_out, or_3_out);
  xor xor_10 (xor_10_out, and_13_out, or_2_out);
  xor xor_11 (xor_11_out, xor_9_out, xor_10_out);
  and and_14 (and_14_out, xor_10_out, xor_9_out);
  xor xor_12 (xor_12_out, xor_11_out, or_10_out);
  and and_15 (and_15_out, xor_12_out, or_4_out);
  and and_16 (and_16_out, xor_11_out, or_5_out);
  and and_17 (and_17_out, or_6_out, and_14_out);
  or or_12 (or_12_out, and_17_out, and_16_out, and_15_out);
  LED led_6 (.in(multiplexer_25_out));
  LED led_7 (.in(multiplexer_28_out));
  LED led_8 (.in(multiplexer_32_out));
  Multiplexer multiplexer_10 (.in0(in_12), .in1(in_13), .out(multiplexer_10_out), .sel(decoder_1_out14));
  xor xor_13 (xor_13_out, multiplexer_10_out, or_3_out);
  xor xor_14 (xor_14_out, xor_13_out, xor_16_out);
  and and_18 (and_18_out, or_10_out, xor_11_out);
  xor xor_15 (xor_15_out, xor_14_out, or_13_out);
  or or_13 (or_13_out, and_18_out, and_14_out);
  not not_5 (not_5_out, or_12_out);
  Multiplexer multiplexer_11 (.in0(or_12_out), .in1(not_5_out), .out(multiplexer_11_out), .sel(or_7_out));
  Multiplexer multiplexer_12 (
    .in0(multiplexer_11_out), .in1(multiplexer_15_out), .out(multiplexer_12_out), .sel(decoder_1_out12));
  Multiplexer multiplexer_13 (
    .in0(multiplexer_7_out), .in1(multiplexer_12_out), .out(multiplexer_13_out), .sel(not_2_out));
  Multiplexer multiplexer_14 (.in0(in_15), .in1(in_16), .out(multiplexer_14_out), .sel(decoder_1_out14));
  and and_19 (and_19_out, in_14, not_1_out);
  xor xor_16 (xor_16_out, and_19_out, or_2_out);
  and and_20 (and_20_out, xor_16_out, xor_13_out);
  and and_21 (and_21_out, or_13_out, xor_14_out);
  or or_14 (or_14_out, and_21_out, and_20_out);
  and and_22 (and_22_out, xor_15_out, or_4_out);
  and and_23 (and_23_out, xor_14_out, or_5_out);
  and and_24 (and_24_out, or_6_out, and_20_out);
  or or_15 (or_15_out, and_24_out, and_23_out, and_22_out);
  not not_6 (not_6_out, or_15_out);
  Multiplexer multiplexer_15 (.in0(or_15_out), .in1(not_6_out), .out(multiplexer_15_out), .sel(or_7_out));
  Multiplexer multiplexer_16 (
    .in0(multiplexer_15_out), .in1(multiplexer_18_out), .out(multiplexer_16_out), .sel(decoder_1_out12));
  Multiplexer multiplexer_17 (
    .in0(multiplexer_12_out), .in1(multiplexer_16_out), .out(multiplexer_17_out), .sel(not_2_out));
  and and_25 (and_25_out, in_17, not_1_out);
  xor xor_17 (xor_17_out, multiplexer_14_out, or_3_out);
  xor xor_18 (xor_18_out, and_25_out, or_2_out);
  xor xor_19 (xor_19_out, xor_17_out, xor_18_out);
  and and_26 (and_26_out, xor_18_out, xor_17_out);
  and and_27 (and_27_out, or_14_out, xor_19_out);
  xor xor_20 (xor_20_out, xor_19_out, or_14_out);
  or or_16 (or_16_out, and_27_out, and_26_out);
  and and_28 (and_28_out, xor_20_out, or_4_out);
  and and_29 (and_29_out, xor_19_out, or_5_out);
  and and_30 (and_30_out, or_6_out, and_26_out);
  or or_17 (or_17_out, and_30_out, and_29_out, and_28_out);
  not not_7 (not_7_out, or_17_out);
  Multiplexer multiplexer_18 (.in0(or_17_out), .in1(not_7_out), .out(multiplexer_18_out), .sel(or_7_out));
  Multiplexer multiplexer_19 (
    .in0(multiplexer_18_out), .in1(multiplexer_23_out), .out(multiplexer_19_out), .sel(decoder_1_out12));
  Multiplexer multiplexer_20 (
    .in0(multiplexer_16_out), .in1(multiplexer_19_out), .out(multiplexer_20_out), .sel(not_2_out));
  Multiplexer multiplexer_21 (.in0(in_18), .in1(in_19), .out(multiplexer_21_out), .sel(decoder_1_out14));
  and and_31 (and_31_out, in_20, not_1_out);
  xor xor_21 (xor_21_out, multiplexer_21_out, or_3_out);
  xor xor_22 (xor_22_out, and_31_out, or_2_out);
  xor xor_23 (xor_23_out, xor_21_out, xor_22_out);
  xor xor_24 (xor_24_out, xor_23_out, or_16_out);
  and and_32 (and_32_out, xor_24_out, or_4_out);
  and and_33 (and_33_out, xor_23_out, or_5_out);
  and and_34 (and_34_out, or_6_out, and_35_out);
  Multiplexer multiplexer_22 (.in0(in_21), .in1(in_22), .out(multiplexer_22_out), .sel(decoder_1_out14));
  xor xor_25 (xor_25_out, multiplexer_22_out, or_3_out);
  and and_35 (and_35_out, xor_22_out, xor_21_out);
  xor xor_26 (xor_26_out, xor_25_out, xor_27_out);
  and and_36 (and_36_out, or_16_out, xor_23_out);
  or or_18 (or_18_out, and_36_out, and_35_out);
  or or_19 (or_19_out, and_34_out, and_33_out, and_32_out);
  not not_8 (not_8_out, or_19_out);
  Multiplexer multiplexer_23 (.in0(or_19_out), .in1(not_8_out), .out(multiplexer_23_out), .sel(or_7_out));
  Multiplexer multiplexer_24 (
    .in0(multiplexer_23_out), .in1(multiplexer_26_out), .out(multiplexer_24_out), .sel(decoder_1_out12));
  Multiplexer multiplexer_25 (
    .in0(multiplexer_19_out), .in1(multiplexer_24_out), .out(multiplexer_25_out), .sel(not_2_out));
  and and_37 (and_37_out, in_23, not_1_out);
  xor xor_27 (xor_27_out, and_37_out, or_2_out);
  and and_38 (and_38_out, xor_27_out, xor_25_out);
  and and_39 (and_39_out, or_18_out, xor_26_out);
  xor xor_28 (xor_28_out, xor_26_out, or_18_out);
  or or_20 (or_20_out, and_39_out, and_38_out);
  and and_40 (and_40_out, xor_28_out, or_4_out);
  and and_41 (and_41_out, xor_26_out, or_5_out);
  and and_42 (and_42_out, or_6_out, and_38_out);
  or or_21 (or_21_out, and_42_out, and_41_out, and_40_out);
  not not_9 (not_9_out, or_21_out);
  Multiplexer multiplexer_26 (.in0(or_21_out), .in1(not_9_out), .out(multiplexer_26_out), .sel(or_7_out));
  Multiplexer multiplexer_27 (
    .in0(multiplexer_26_out), .in1(multiplexer_30_out), .out(multiplexer_27_out), .sel(decoder_1_out12));
  Multiplexer multiplexer_28 (
    .in0(multiplexer_24_out), .in1(multiplexer_27_out), .out(multiplexer_28_out), .sel(not_2_out));
  Multiplexer multiplexer_29 (.in0(in_24), .in1(in_25), .out(multiplexer_29_out), .sel(decoder_1_out14));
  and and_43 (and_43_out, in_26, not_1_out);
  xor xor_29 (xor_29_out, multiplexer_29_out, or_3_out);
  xor xor_30 (xor_30_out, and_43_out, or_2_out);
  xor xor_31 (xor_31_out, xor_29_out, xor_30_out);
  and and_44 (and_44_out, xor_30_out, xor_29_out);
  and and_45 (and_45_out, or_20_out, xor_31_out);
  xor xor_32 (xor_32_out, xor_31_out, or_20_out);
  and and_46 (and_46_out, xor_32_out, or_4_out);
  and and_47 (and_47_out, xor_31_out, or_5_out);
  and and_48 (and_48_out, or_6_out, and_44_out);
  or or_22 (or_22_out, and_48_out, and_47_out, and_46_out);
  Multiplexer multiplexer_30 (.in0(or_22_out), .in1(not_10_out), .out(multiplexer_30_out), .sel(or_7_out));
  Multiplexer multiplexer_31 (.in0(multiplexer_30_out), .in1(in_46), .out(multiplexer_31_out), .sel(decoder_1_out12));
  Multiplexer multiplexer_32 (
    .in0(multiplexer_27_out), .in1(multiplexer_31_out), .out(multiplexer_32_out), .sel(not_2_out));
  or or_23 (or_23_out, and_45_out, and_44_out);
  not not_10 (not_10_out, or_22_out);
  or or_24 (or_24_out, multiplexer_32_out, multiplexer_28_out, multiplexer_25_out, multiplexer_20_out, multiplexer_17_out, multiplexer_13_out, multiplexer_8_out, multiplexer_5_out);
  not not_11 (not_11_out, or_24_out);
  LED led_9 (.in(not_11_out));
  LED led_10 (.in(or_14_out));
  LED led_11 (.in(or_23_out));
  or or_25 (or_25_out[0], ADD__0001, OR__0011, XOR__0101, NOR__0111, XNOR__1001, in_56, in_58);
  or or_26 (or_25_out[1], SUB__0010, OR__0011, NOT__0110, NOR__0111, in_55, in_56, in_59);
  or or_27 (or_25_out[2], AND__0100, XOR__0101, NOT__0110, NOR__0111, in_57, in_58, in_59);
  or or_28 (or_25_out[3], NAND__1000, XNOR__1001, in_55, in_56, in_57, in_58, in_59);
  Decoder #(.select(4)) decoder_2 (
    .out1(decoder_2_out1), .out2(decoder_2_out2), .out3(decoder_2_out3), .out4(decoder_2_out4),
    .out5(decoder_2_out5), .out6(decoder_2_out6), .out7(decoder_2_out7), .out8(decoder_2_out8),
    .out9(decoder_2_out9), .out10(decoder_2_out10), .out11(decoder_2_out11), .out12(decoder_2_out12),
    .out13(decoder_2_out13), .out14(decoder_2_out14), .sel(or_25_out), .en(in_60));  // open: out0, out15
  or or_29 (or_29_out, decoder_2_out13, decoder_2_out12, decoder_2_out6);
  not not_12 (not_12_out, or_29_out);
  or or_30 (or_30_out, decoder_2_out2, decoder_2_out11, decoder_2_out10, decoder_2_out3, decoder_2_out7);
  or or_31 (or_31_out, decoder_2_out3, decoder_2_out7, decoder_2_out6);
  Multiplexer multiplexer_33 (.in0(in_32), .in1(in_61), .out(multiplexer_33_out), .sel(decoder_2_out14));
  and and_49 (and_49_out, in_40, not_12_out);
  xor xor_33 (xor_33_out, multiplexer_33_out, or_31_out);
  xor xor_34 (xor_34_out, and_49_out, or_30_out);
  xor xor_35 (xor_35_out, xor_33_out, xor_34_out);
  and and_50 (and_50_out, xor_34_out, xor_33_out);
  xor xor_36 (xor_36_out, xor_35_out, decoder_2_out2);
  or or_32 (or_32_out, decoder_2_out1, decoder_2_out2, decoder_2_out6, decoder_2_out12);
  and and_51 (and_51_out, xor_36_out, or_32_out);
  or or_33 (or_33_out, decoder_2_out5, decoder_2_out13, decoder_2_out9, decoder_2_out14);
  and and_52 (and_52_out, xor_35_out, or_33_out);
  or or_34 (or_34_out, decoder_2_out8, decoder_2_out3, decoder_2_out11, decoder_2_out4, decoder_2_out7, decoder_2_out10);
  and and_53 (and_53_out, or_34_out, and_50_out);
  or or_35 (or_35_out, and_53_out, and_52_out, and_51_out);
  or or_36 (or_36_out, decoder_2_out8, decoder_2_out10, decoder_2_out3, decoder_2_out9);
  not not_13 (not_13_out, decoder_2_out13);
  Multiplexer multiplexer_34 (.in0(in_31), .in1(in_62), .out(multiplexer_34_out), .sel(decoder_2_out14));
  xor xor_37 (xor_37_out, multiplexer_34_out, or_31_out);
  xor xor_38 (xor_38_out, xor_37_out, xor_40_out);
  and and_54 (and_54_out, decoder_2_out2, xor_35_out);
  xor xor_39 (xor_39_out, xor_38_out, or_37_out);
  or or_37 (or_37_out, and_54_out, and_50_out);
  not not_14 (not_14_out, or_35_out);
  Multiplexer multiplexer_35 (.in0(or_35_out), .in1(not_14_out), .out(multiplexer_35_out), .sel(or_36_out));
  Multiplexer multiplexer_36 (
    .in0(multiplexer_35_out), .in1(multiplexer_39_out), .out(multiplexer_36_out), .sel(decoder_2_out12));
  Multiplexer multiplexer_37 (.in0(in_70), .in1(multiplexer_36_out), .out(multiplexer_37_out[0]), .sel(not_13_out));
  LED led_12 (.in(multiplexer_37_out[0]));
  LED led_13 (.in(multiplexer_37_out[1]));
  LED led_14 (.in(multiplexer_37_out[2]));
  Multiplexer multiplexer_38 (.in0(in_30), .in1(in_63), .out(multiplexer_38_out), .sel(decoder_2_out14));
  and and_55 (and_55_out, in_39, not_12_out);
  xor xor_40 (xor_40_out, and_55_out, or_30_out);
  and and_56 (and_56_out, xor_40_out, xor_37_out);
  and and_57 (and_57_out, or_37_out, xor_38_out);
  or or_38 (or_38_out, and_57_out, and_56_out);
  and and_58 (and_58_out, xor_39_out, or_32_out);
  and and_59 (and_59_out, xor_38_out, or_33_out);
  and and_60 (and_60_out, or_34_out, and_56_out);
  or or_39 (or_39_out, and_60_out, and_59_out, and_58_out);
  not not_15 (not_15_out, or_39_out);
  Multiplexer multiplexer_39 (.in0(or_39_out), .in1(not_15_out), .out(multiplexer_39_out), .sel(or_36_out));
  Multiplexer multiplexer_40 (
    .in0(multiplexer_39_out), .in1(multiplexer_42_out), .out(multiplexer_40_out), .sel(decoder_2_out12));
  Multiplexer multiplexer_41 (
    .in0(multiplexer_36_out), .in1(multiplexer_40_out), .out(multiplexer_37_out[1]), .sel(not_13_out));
  LED led_15 (.in(multiplexer_37_out[3]));
  LED led_16 (.in(multiplexer_37_out[4]));
  LED led_17 (.in(multiplexer_37_out[5]));
  // Binary_to_BCD_converter #(.binvalue(8)) binary_to_bcd_converter_1: pin names not known; wires that end beside it: {in_1, in_2, in_27, in_28, in_29, in_30, in_31, in_32}, binary_to_bcd_converter_1_p2, binary_to_bcd_converter_1_p3, binary_to_bcd_converter_1_p4
  // Binary_to_BCD_converter #(.binvalue(8)) binary_to_bcd_converter_2: pin names not known; wires that end beside it: {in_33, in_34, in_35, in_36, INPUT__B, in_38, in_39, in_40}, binary_to_bcd_converter_2_p2, binary_to_bcd_converter_2_p3, binary_to_bcd_converter_2_p4
  and and_61 (and_61_out, in_38, not_12_out);
  xor xor_41 (xor_41_out, multiplexer_38_out, or_31_out);
  xor xor_42 (xor_42_out, and_61_out, or_30_out);
  xor xor_43 (xor_43_out, xor_41_out, xor_42_out);
  and and_62 (and_62_out, xor_42_out, xor_41_out);
  and and_63 (and_63_out, or_38_out, xor_43_out);
  xor xor_44 (xor_44_out, xor_43_out, or_38_out);
  or or_40 (or_40_out, and_63_out, and_62_out);
  and and_64 (and_64_out, xor_44_out, or_32_out);
  and and_65 (and_65_out, xor_43_out, or_33_out);
  and and_66 (and_66_out, or_34_out, and_62_out);
  or or_41 (or_41_out, and_66_out, and_65_out, and_64_out);
  not not_16 (not_16_out, or_41_out);
  Multiplexer multiplexer_42 (.in0(or_41_out), .in1(not_16_out), .out(multiplexer_42_out), .sel(or_36_out));
  Multiplexer multiplexer_43 (
    .in0(multiplexer_42_out), .in1(multiplexer_47_out), .out(multiplexer_43_out), .sel(decoder_2_out12));
  Multiplexer multiplexer_44 (
    .in0(multiplexer_40_out), .in1(multiplexer_43_out), .out(multiplexer_37_out[2]), .sel(not_13_out));
  LED led_18 (.in(multiplexer_37_out[6]));
  LED led_19 (.in(multiplexer_37_out[7]));
  Multiplexer multiplexer_45 (.in0(in_29), .in1(USER_INPUT), .out(multiplexer_45_out), .sel(decoder_2_out14));
  and and_67 (and_67_out, INPUT__B, not_12_out);
  xor xor_45 (xor_45_out, multiplexer_45_out, or_31_out);
  xor xor_46 (xor_46_out, and_67_out, or_30_out);
  xor xor_47 (xor_47_out, xor_45_out, xor_46_out);
  xor xor_48 (xor_48_out, xor_47_out, or_40_out);
  and and_68 (and_68_out, xor_48_out, or_32_out);
  and and_69 (and_69_out, xor_47_out, or_33_out);
  and and_70 (and_70_out, or_34_out, and_71_out);
  Multiplexer multiplexer_46 (.in0(in_28), .in1(in_65), .out(multiplexer_46_out), .sel(decoder_2_out14));
  xor xor_49 (xor_49_out, multiplexer_46_out, or_31_out);
  and and_71 (and_71_out, xor_46_out, xor_45_out);
  xor xor_50 (xor_50_out, xor_49_out, xor_51_out);
  and and_72 (and_72_out, or_40_out, xor_47_out);
  or or_42 (or_42_out, and_72_out, and_71_out);
  or or_43 (or_43_out, and_70_out, and_69_out, and_68_out);
  not not_17 (not_17_out, or_43_out);
  Multiplexer multiplexer_47 (.in0(or_43_out), .in1(not_17_out), .out(multiplexer_47_out), .sel(or_36_out));
  Multiplexer multiplexer_48 (
    .in0(multiplexer_47_out), .in1(multiplexer_50_out), .out(multiplexer_48_out), .sel(decoder_2_out12));
  Multiplexer multiplexer_49 (
    .in0(multiplexer_43_out), .in1(multiplexer_48_out), .out(multiplexer_37_out[3]), .sel(not_13_out));
  and and_73 (and_73_out, in_36, not_12_out);
  xor xor_51 (xor_51_out, and_73_out, or_30_out);
  and and_74 (and_74_out, xor_51_out, xor_49_out);
  and and_75 (and_75_out, or_42_out, xor_50_out);
  xor xor_52 (xor_52_out, xor_50_out, or_42_out);
  or or_44 (or_44_out, and_75_out, and_74_out);
  and and_76 (and_76_out, xor_52_out, or_32_out);
  and and_77 (and_77_out, xor_50_out, or_33_out);
  and and_78 (and_78_out, or_34_out, and_74_out);
  or or_45 (or_45_out, and_78_out, and_77_out, and_76_out);
  not not_18 (not_18_out, or_45_out);
  Multiplexer multiplexer_50 (.in0(or_45_out), .in1(not_18_out), .out(multiplexer_50_out), .sel(or_36_out));
  Multiplexer multiplexer_51 (
    .in0(multiplexer_50_out), .in1(multiplexer_54_out), .out(multiplexer_51_out), .sel(decoder_2_out12));
  Multiplexer multiplexer_52 (
    .in0(multiplexer_48_out), .in1(multiplexer_51_out), .out(multiplexer_37_out[4]), .sel(not_13_out));
  _7_Segment_Display u_7_segment_display_1 (
    .g(bcd_to_7_segment_decoder_1_p1), .f(bcd_to_7_segment_decoder_1_p3), .a(bcd_to_7_segment_decoder_1_p6),
    .b(bcd_to_7_segment_decoder_1_p8), .e(bcd_to_7_segment_decoder_1_p2), .d(bcd_to_7_segment_decoder_1_p4),
    .c(bcd_to_7_segment_decoder_1_p7));  // open: dp
  // BCD_to_7_Segment_decoder bcd_to_7_segment_decoder_1: pin names not known; wires that end beside it: bcd_to_7_segment_decoder_1_p1, bcd_to_7_segment_decoder_1_p2, bcd_to_7_segment_decoder_1_p3, bcd_to_7_segment_decoder_1_p4, binary_to_bcd_converter_1_p2, bcd_to_7_segment_decoder_1_p6, bcd_to_7_segment_decoder_1_p7, bcd_to_7_segment_decoder_1_p8
  _7_Segment_Display u_7_segment_display_2 (
    .g(bcd_to_7_segment_decoder_2_p1), .f(bcd_to_7_segment_decoder_2_p3), .a(bcd_to_7_segment_decoder_2_p6),
    .b(bcd_to_7_segment_decoder_2_p8), .e(bcd_to_7_segment_decoder_2_p2), .d(bcd_to_7_segment_decoder_2_p4),
    .c(bcd_to_7_segment_decoder_2_p7));  // open: dp
  // BCD_to_7_Segment_decoder bcd_to_7_segment_decoder_2: pin names not known; wires that end beside it: bcd_to_7_segment_decoder_2_p1, bcd_to_7_segment_decoder_2_p2, bcd_to_7_segment_decoder_2_p3, bcd_to_7_segment_decoder_2_p4, binary_to_bcd_converter_2_p2, bcd_to_7_segment_decoder_2_p6, bcd_to_7_segment_decoder_2_p7, bcd_to_7_segment_decoder_2_p8
  Multiplexer multiplexer_53 (.in0(in_27), .in1(in_66), .out(multiplexer_53_out), .sel(decoder_2_out14));
  and and_79 (and_79_out, in_35, not_12_out);
  xor xor_53 (xor_53_out, multiplexer_53_out, or_31_out);
  xor xor_54 (xor_54_out, and_79_out, or_30_out);
  xor xor_55 (xor_55_out, xor_53_out, xor_54_out);
  and and_80 (and_80_out, xor_54_out, xor_53_out);
  and and_81 (and_81_out, or_44_out, xor_55_out);
  xor xor_56 (xor_56_out, xor_55_out, or_44_out);
  and and_82 (and_82_out, xor_56_out, or_32_out);
  and and_83 (and_83_out, xor_55_out, or_33_out);
  and and_84 (and_84_out, or_34_out, and_80_out);
  or or_46 (or_46_out, and_84_out, and_83_out, and_82_out);
  Multiplexer multiplexer_54 (.in0(or_46_out), .in1(not_19_out), .out(multiplexer_54_out), .sel(or_36_out));
  Multiplexer multiplexer_55 (
    .in0(multiplexer_54_out), .in1(multiplexer_59_out), .out(multiplexer_55_out), .sel(decoder_2_out12));
  Multiplexer multiplexer_56 (
    .in0(multiplexer_51_out), .in1(multiplexer_55_out), .out(multiplexer_37_out[5]), .sel(not_13_out));
  // Binary_to_BCD_converter #(.binvalue(8)) binary_to_bcd_converter_3: pin names not known; wires that end beside it: multiplexer_37_out, binary_to_bcd_converter_3_p2, binary_to_bcd_converter_3_p3, binary_to_bcd_converter_3_p4
  _7_Segment_Display u_7_segment_display_3 (
    .g(bcd_to_7_segment_decoder_3_p1), .f(bcd_to_7_segment_decoder_3_p3), .a(bcd_to_7_segment_decoder_3_p6),
    .b(bcd_to_7_segment_decoder_3_p8), .e(bcd_to_7_segment_decoder_3_p2), .d(bcd_to_7_segment_decoder_3_p4),
    .c(bcd_to_7_segment_decoder_3_p7));  // open: dp
  // BCD_to_7_Segment_decoder bcd_to_7_segment_decoder_3: pin names not known; wires that end beside it: bcd_to_7_segment_decoder_3_p1, bcd_to_7_segment_decoder_3_p2, bcd_to_7_segment_decoder_3_p3, bcd_to_7_segment_decoder_3_p4, binary_to_bcd_converter_1_p3, bcd_to_7_segment_decoder_3_p6, bcd_to_7_segment_decoder_3_p7, bcd_to_7_segment_decoder_3_p8
  _7_Segment_Display u_7_segment_display_4 (
    .g(bcd_to_7_segment_decoder_4_p1), .f(bcd_to_7_segment_decoder_4_p3), .a(bcd_to_7_segment_decoder_4_p6),
    .b(bcd_to_7_segment_decoder_4_p8), .e(bcd_to_7_segment_decoder_4_p2), .d(bcd_to_7_segment_decoder_4_p4),
    .c(bcd_to_7_segment_decoder_4_p7));  // open: dp
  // BCD_to_7_Segment_decoder bcd_to_7_segment_decoder_4: pin names not known; wires that end beside it: bcd_to_7_segment_decoder_4_p1, bcd_to_7_segment_decoder_4_p2, bcd_to_7_segment_decoder_4_p3, bcd_to_7_segment_decoder_4_p4, binary_to_bcd_converter_2_p3, bcd_to_7_segment_decoder_4_p6, bcd_to_7_segment_decoder_4_p7, bcd_to_7_segment_decoder_4_p8
  Multiplexer multiplexer_57 (.in0(in_2), .in1(in_67), .out(multiplexer_57_out), .sel(decoder_2_out14));
  and and_85 (and_85_out, in_34, not_12_out);
  xor xor_57 (xor_57_out, multiplexer_57_out, or_31_out);
  xor xor_58 (xor_58_out, xor_57_out, xor_60_out);
  xor xor_59 (xor_59_out, xor_58_out, or_47_out);
  or or_47 (or_47_out, and_81_out, and_80_out);
  and and_86 (and_86_out, xor_59_out, or_32_out);
  and and_87 (and_87_out, or_34_out, and_88_out);
  not not_19 (not_19_out, or_46_out);
  Multiplexer multiplexer_58 (.in0(in_1), .in1(in_68), .out(multiplexer_58_out), .sel(decoder_2_out14));
  xor xor_60 (xor_60_out, and_85_out, or_30_out);
  xor xor_61 (xor_61_out, multiplexer_58_out, or_31_out);
  and and_88 (and_88_out, xor_60_out, xor_57_out);
  and and_89 (and_89_out, or_47_out, xor_58_out);
  or or_48 (or_48_out, and_89_out, and_88_out);
  and and_90 (and_90_out, xor_58_out, or_33_out);
  or or_49 (or_49_out, and_87_out, and_90_out, and_86_out);
  not not_20 (not_20_out, or_49_out);
  Multiplexer multiplexer_59 (.in0(or_49_out), .in1(not_20_out), .out(multiplexer_59_out), .sel(or_36_out));
  Multiplexer multiplexer_60 (
    .in0(multiplexer_59_out), .in1(multiplexer_62_out), .out(multiplexer_60_out), .sel(decoder_2_out12));
  Multiplexer multiplexer_61 (
    .in0(multiplexer_55_out), .in1(multiplexer_60_out), .out(multiplexer_37_out[6]), .sel(not_13_out));
  _7_Segment_Display u_7_segment_display_5 (
    .g(bcd_to_7_segment_decoder_5_p1), .f(bcd_to_7_segment_decoder_5_p3), .a(bcd_to_7_segment_decoder_5_p6),
    .b(bcd_to_7_segment_decoder_5_p8), .e(bcd_to_7_segment_decoder_5_p2), .d(bcd_to_7_segment_decoder_5_p4),
    .c(bcd_to_7_segment_decoder_5_p7));  // open: dp
  // BCD_to_7_Segment_decoder bcd_to_7_segment_decoder_5: pin names not known; wires that end beside it: bcd_to_7_segment_decoder_5_p1, bcd_to_7_segment_decoder_5_p2, bcd_to_7_segment_decoder_5_p3, bcd_to_7_segment_decoder_5_p4, binary_to_bcd_converter_1_p4, bcd_to_7_segment_decoder_5_p6, bcd_to_7_segment_decoder_5_p7, bcd_to_7_segment_decoder_5_p8
  _7_Segment_Display u_7_segment_display_6 (
    .g(bcd_to_7_segment_decoder_6_p1), .f(bcd_to_7_segment_decoder_6_p3), .a(bcd_to_7_segment_decoder_6_p6),
    .b(bcd_to_7_segment_decoder_6_p8), .e(bcd_to_7_segment_decoder_6_p2), .d(bcd_to_7_segment_decoder_6_p4),
    .c(bcd_to_7_segment_decoder_6_p7));  // open: dp
  // BCD_to_7_Segment_decoder bcd_to_7_segment_decoder_6: pin names not known; wires that end beside it: bcd_to_7_segment_decoder_6_p1, bcd_to_7_segment_decoder_6_p2, bcd_to_7_segment_decoder_6_p3, bcd_to_7_segment_decoder_6_p4, binary_to_bcd_converter_2_p4, bcd_to_7_segment_decoder_6_p6, bcd_to_7_segment_decoder_6_p7, bcd_to_7_segment_decoder_6_p8
  and and_91 (and_91_out, in_33, not_12_out);
  xor xor_62 (xor_62_out, and_91_out, or_30_out);
  xor xor_63 (xor_63_out, xor_61_out, xor_62_out);
  and and_92 (and_92_out, xor_62_out, xor_61_out);
  and and_93 (and_93_out, or_48_out, xor_63_out);
  xor xor_64 (xor_64_out, xor_63_out, or_48_out);
  or or_50 (or_50_out, and_93_out, and_92_out);
  and and_94 (and_94_out, xor_64_out, or_32_out);
  and and_95 (and_95_out, xor_63_out, or_33_out);
  and and_96 (and_96_out, or_34_out, and_92_out);
  or or_51 (or_51_out, and_96_out, and_95_out, and_94_out);
  not not_21 (not_21_out, or_51_out);
  Multiplexer multiplexer_62 (.in0(or_51_out), .in1(not_21_out), .out(multiplexer_62_out), .sel(or_36_out));
  Multiplexer multiplexer_63 (.in0(multiplexer_62_out), .in1(in_69), .out(multiplexer_63_out), .sel(decoder_2_out12));
  Multiplexer multiplexer_64 (
    .in0(multiplexer_60_out), .in1(multiplexer_63_out), .out(multiplexer_37_out[7]), .sel(not_13_out));
  or or_52 (or_52_out, multiplexer_37_out[7], multiplexer_37_out[6], multiplexer_37_out[5], multiplexer_37_out[4], multiplexer_37_out[3], multiplexer_37_out[2], multiplexer_37_out[1], multiplexer_37_out[0]);
  not not_22 (not_22_out, or_52_out);
  _7_Segment_Display u_7_segment_display_7 (
    .g(bcd_to_7_segment_decoder_7_p1), .f(bcd_to_7_segment_decoder_7_p3), .a(bcd_to_7_segment_decoder_7_p6),
    .b(bcd_to_7_segment_decoder_7_p8), .e(bcd_to_7_segment_decoder_7_p2), .d(bcd_to_7_segment_decoder_7_p4),
    .c(bcd_to_7_segment_decoder_7_p7));  // open: dp
  // BCD_to_7_Segment_decoder bcd_to_7_segment_decoder_7: pin names not known; wires that end beside it: bcd_to_7_segment_decoder_7_p1, bcd_to_7_segment_decoder_7_p2, bcd_to_7_segment_decoder_7_p3, bcd_to_7_segment_decoder_7_p4, binary_to_bcd_converter_3_p2, bcd_to_7_segment_decoder_7_p6, bcd_to_7_segment_decoder_7_p7, bcd_to_7_segment_decoder_7_p8
  // Binary_to_BCD_converter #(.binvalue(8)) binary_to_bcd_converter_4: pin names not known; wires that end beside it: {in_68, in_67, in_66, in_65, USER_INPUT, in_63, in_62, in_61}, binary_to_bcd_converter_4_p2, binary_to_bcd_converter_4_p3, binary_to_bcd_converter_4_p4
  LED led_20 (.in(or_50_out));
  LED led_21 (.in(or_42_out));
  LED led_22 (.in(not_22_out));
  _7_Segment_Display u_7_segment_display_8 (
    .g(bcd_to_7_segment_decoder_8_p1), .f(bcd_to_7_segment_decoder_8_p3), .a(bcd_to_7_segment_decoder_8_p6),
    .b(bcd_to_7_segment_decoder_8_p8), .e(bcd_to_7_segment_decoder_8_p2), .d(bcd_to_7_segment_decoder_8_p4),
    .c(bcd_to_7_segment_decoder_8_p7));  // open: dp
  // BCD_to_7_Segment_decoder bcd_to_7_segment_decoder_8: pin names not known; wires that end beside it: bcd_to_7_segment_decoder_8_p1, bcd_to_7_segment_decoder_8_p2, bcd_to_7_segment_decoder_8_p3, bcd_to_7_segment_decoder_8_p4, binary_to_bcd_converter_3_p3, bcd_to_7_segment_decoder_8_p6, bcd_to_7_segment_decoder_8_p7, bcd_to_7_segment_decoder_8_p8
  _7_Segment_Display u_7_segment_display_9 (
    .g(bcd_to_7_segment_decoder_9_p1), .f(bcd_to_7_segment_decoder_9_p3), .a(bcd_to_7_segment_decoder_9_p6),
    .b(bcd_to_7_segment_decoder_9_p8), .e(bcd_to_7_segment_decoder_9_p2), .d(bcd_to_7_segment_decoder_9_p4),
    .c(bcd_to_7_segment_decoder_9_p7));  // open: dp
  // BCD_to_7_Segment_decoder bcd_to_7_segment_decoder_9: pin names not known; wires that end beside it: bcd_to_7_segment_decoder_9_p1, bcd_to_7_segment_decoder_9_p2, bcd_to_7_segment_decoder_9_p3, bcd_to_7_segment_decoder_9_p4, binary_to_bcd_converter_3_p4, bcd_to_7_segment_decoder_9_p6, bcd_to_7_segment_decoder_9_p7, bcd_to_7_segment_decoder_9_p8
  _7_Segment_Display u_7_segment_display_10 (
    .g(bcd_to_7_segment_decoder_10_p1), .f(bcd_to_7_segment_decoder_10_p3),
    .a(bcd_to_7_segment_decoder_10_p6), .b(bcd_to_7_segment_decoder_10_p8),
    .e(bcd_to_7_segment_decoder_10_p2), .d(bcd_to_7_segment_decoder_10_p4), .c(bcd_to_7_segment_decoder_10_p7));  // open: dp
  // BCD_to_7_Segment_decoder bcd_to_7_segment_decoder_10: pin names not known; wires that end beside it: bcd_to_7_segment_decoder_10_p1, bcd_to_7_segment_decoder_10_p2, bcd_to_7_segment_decoder_10_p3, bcd_to_7_segment_decoder_10_p4, binary_to_bcd_converter_4_p2, bcd_to_7_segment_decoder_10_p6, bcd_to_7_segment_decoder_10_p7, bcd_to_7_segment_decoder_10_p8
  _7_Segment_Display u_7_segment_display_11 (
    .g(bcd_to_7_segment_decoder_11_p1), .f(bcd_to_7_segment_decoder_11_p3),
    .a(bcd_to_7_segment_decoder_11_p6), .b(bcd_to_7_segment_decoder_11_p8),
    .e(bcd_to_7_segment_decoder_11_p2), .d(bcd_to_7_segment_decoder_11_p4), .c(bcd_to_7_segment_decoder_11_p7));  // open: dp
  // BCD_to_7_Segment_decoder bcd_to_7_segment_decoder_11: pin names not known; wires that end beside it: bcd_to_7_segment_decoder_11_p1, bcd_to_7_segment_decoder_11_p2, bcd_to_7_segment_decoder_11_p3, bcd_to_7_segment_decoder_11_p4, binary_to_bcd_converter_4_p3, bcd_to_7_segment_decoder_11_p6, bcd_to_7_segment_decoder_11_p7, bcd_to_7_segment_decoder_11_p8
  _7_Segment_Display u_7_segment_display_12 (
    .g(bcd_to_7_segment_decoder_12_p1), .f(bcd_to_7_segment_decoder_12_p3),
    .a(bcd_to_7_segment_decoder_12_p6), .b(bcd_to_7_segment_decoder_12_p8),
    .e(bcd_to_7_segment_decoder_12_p2), .d(bcd_to_7_segment_decoder_12_p4), .c(bcd_to_7_segment_decoder_12_p7));  // open: dp
  // BCD_to_7_Segment_decoder bcd_to_7_segment_decoder_12: pin names not known; wires that end beside it: bcd_to_7_segment_decoder_12_p1, bcd_to_7_segment_decoder_12_p2, bcd_to_7_segment_decoder_12_p3, bcd_to_7_segment_decoder_12_p4, binary_to_bcd_converter_4_p4, bcd_to_7_segment_decoder_12_p6, bcd_to_7_segment_decoder_12_p7, bcd_to_7_segment_decoder_12_p8

  // Notes on the sheet:
  //   OPCODES:
  //   NOP: 0000
  //   ADD: 0001
  //   SUB: 0010
  //   OR: 0011
  //   AND: 0100
  //   XOR: 0101
  //   NOT: 0110
  //   NOR: 0111
  //   NAND: 1000
  //   XNOR: 1001
  //   IMPLIES: 1010
  //   NIMPLIES: 1011
  //   LEFT SHIFT: 1100
  //   RIGHT SHIFT: 1101
  //   USER INPUT: 1110
  //   OUTPUT
  //   _________________________________________________________________________________________________________________________________________________________________________________________
  //   _________________________________________________________________________________________________________________________________________________________________________________________
  //   1) ZERO FLAG
  //   2) AUXILARY CARRY
  //   3) OVERFLOW
  //   INPUT -A 
  //   NOP: 0000
  //   IMPLIES: 1010
  //   NIMPLIES: 1011
  //   LEFT SHIFT: 1100
  //   RIGHT SHIFT: 1101
  //   USER INPUT: 1110
  //   Enable Operation
  //   A
  //   B
  //   3) OVERFLOW
  //   2) AUXILARY CARRY
  //   1) ZERO FLAG
  //   OUTPUT
  //   USER-INPUT
endmodule
