// Logisim project Digital_Vote_Register.circ as structural Verilog: 1 circuit, main circuit main
module main (
  input  Criteria__1,
  input  Criteria__2,
  input  Criteria__3,
  input  Candidate__1,
  input  Candidate__2,
  input  Candidate__3,
  input  Candidate__4
);

  wire and_1_out, and_2_out, and_3_out, and_4_out, and_5_out, and_6_out, and_7_out, and_8_out, and_9_out,
       bcd_to_7_segment_decoder_1_p1, bcd_to_7_segment_decoder_1_p2, bcd_to_7_segment_decoder_1_p3,
       bcd_to_7_segment_decoder_1_p4, bcd_to_7_segment_decoder_1_p6, bcd_to_7_segment_decoder_1_p7,
       bcd_to_7_segment_decoder_1_p8, bcd_to_7_segment_decoder_2_p1, bcd_to_7_segment_decoder_2_p2,
       bcd_to_7_segment_decoder_2_p3, bcd_to_7_segment_decoder_2_p4, bcd_to_7_segment_decoder_2_p6,
       bcd_to_7_segment_decoder_2_p7, bcd_to_7_segment_decoder_2_p8, bcd_to_7_segment_decoder_3_p1,
       bcd_to_7_segment_decoder_3_p2, bcd_to_7_segment_decoder_3_p3, bcd_to_7_segment_decoder_3_p4,
       bcd_to_7_segment_decoder_3_p6, bcd_to_7_segment_decoder_3_p7, bcd_to_7_segment_decoder_3_p8,
       bcd_to_7_segment_decoder_4_p1, bcd_to_7_segment_decoder_4_p2, bcd_to_7_segment_decoder_4_p3,
       bcd_to_7_segment_decoder_4_p4, bcd_to_7_segment_decoder_4_p6, bcd_to_7_segment_decoder_4_p7,
       bcd_to_7_segment_decoder_4_p8, bcd_to_7_segment_decoder_5_p1, bcd_to_7_segment_decoder_5_p2,
       bcd_to_7_segment_decoder_5_p3, bcd_to_7_segment_decoder_5_p4, bcd_to_7_segment_decoder_5_p6,
       bcd_to_7_segment_decoder_5_p7, bcd_to_7_segment_decoder_5_p8, bcd_to_7_segment_decoder_6_p1,
       bcd_to_7_segment_decoder_6_p2, bcd_to_7_segment_decoder_6_p3, bcd_to_7_segment_decoder_6_p4,
       bcd_to_7_segment_decoder_6_p6, bcd_to_7_segment_decoder_6_p7, bcd_to_7_segment_decoder_6_p8,
       bcd_to_7_segment_decoder_7_p1, bcd_to_7_segment_decoder_7_p2, bcd_to_7_segment_decoder_7_p3,
       bcd_to_7_segment_decoder_7_p4, bcd_to_7_segment_decoder_7_p6, bcd_to_7_segment_decoder_7_p7,
       bcd_to_7_segment_decoder_7_p8, bcd_to_7_segment_decoder_8_p1, bcd_to_7_segment_decoder_8_p2,
       bcd_to_7_segment_decoder_8_p3, bcd_to_7_segment_decoder_8_p4, bcd_to_7_segment_decoder_8_p6,
       bcd_to_7_segment_decoder_8_p7, bcd_to_7_segment_decoder_8_p8, bcd_to_7_segment_decoder_9_p1,
       bcd_to_7_segment_decoder_9_p2, bcd_to_7_segment_decoder_9_p3, bcd_to_7_segment_decoder_9_p4,
       bcd_to_7_segment_decoder_9_p6, bcd_to_7_segment_decoder_9_p7, bcd_to_7_segment_decoder_9_p8,
       bcd_to_7_segment_decoder_10_p1, bcd_to_7_segment_decoder_10_p2, bcd_to_7_segment_decoder_10_p3,
       bcd_to_7_segment_decoder_10_p4, bcd_to_7_segment_decoder_10_p6, bcd_to_7_segment_decoder_10_p7,
       bcd_to_7_segment_decoder_10_p8, bcd_to_7_segment_decoder_11_p1, bcd_to_7_segment_decoder_11_p2,
       bcd_to_7_segment_decoder_11_p3, bcd_to_7_segment_decoder_11_p4, bcd_to_7_segment_decoder_11_p6,
       bcd_to_7_segment_decoder_11_p7, bcd_to_7_segment_decoder_11_p8, bcd_to_7_segment_decoder_12_p1,
       bcd_to_7_segment_decoder_12_p2, bcd_to_7_segment_decoder_12_p3, bcd_to_7_segment_decoder_12_p4,
       bcd_to_7_segment_decoder_12_p6, bcd_to_7_segment_decoder_12_p7, bcd_to_7_segment_decoder_12_p8,
       bcd_to_7_segment_decoder_13_p1, bcd_to_7_segment_decoder_13_p2, bcd_to_7_segment_decoder_13_p3,
       bcd_to_7_segment_decoder_13_p4, bcd_to_7_segment_decoder_13_p6, bcd_to_7_segment_decoder_13_p7,
       bcd_to_7_segment_decoder_13_p8, bcd_to_7_segment_decoder_14_p1, bcd_to_7_segment_decoder_14_p2,
       bcd_to_7_segment_decoder_14_p3, bcd_to_7_segment_decoder_14_p4, bcd_to_7_segment_decoder_14_p6,
       bcd_to_7_segment_decoder_14_p7, bcd_to_7_segment_decoder_14_p8, bcd_to_7_segment_decoder_15_p1,
       bcd_to_7_segment_decoder_15_p2, bcd_to_7_segment_decoder_15_p3, bcd_to_7_segment_decoder_15_p4,
       bcd_to_7_segment_decoder_15_p6, bcd_to_7_segment_decoder_15_p7, bcd_to_7_segment_decoder_15_p8,
       bcd_to_7_segment_decoder_16_p1, bcd_to_7_segment_decoder_16_p2, bcd_to_7_segment_decoder_16_p3,
       bcd_to_7_segment_decoder_16_p4, bcd_to_7_segment_decoder_16_p6, bcd_to_7_segment_decoder_16_p7,
       bcd_to_7_segment_decoder_16_p8, binary_to_bcd_converter_1_p2, binary_to_bcd_converter_1_p3,
       binary_to_bcd_converter_1_p4, binary_to_bcd_converter_1_p5, binary_to_bcd_converter_2_p2,
       binary_to_bcd_converter_2_p3, binary_to_bcd_converter_2_p4, binary_to_bcd_converter_2_p5,
       binary_to_bcd_converter_3_p2, binary_to_bcd_converter_3_p3, binary_to_bcd_converter_3_p4,
       binary_to_bcd_converter_3_p5, binary_to_bcd_converter_4_p2, binary_to_bcd_converter_4_p3,
       binary_to_bcd_converter_4_p4, binary_to_bcd_converter_4_p5, button_1_out, button_2_out, button_3_out,
       d_ff_1_q, d_ff_1_qn, d_ff_2_q, d_ff_2_qn, d_ff_3_q, d_ff_3_qn, d_ff_4_q, d_ff_4_qn, d_ff_5_q,
       d_ff_5_qn, d_ff_6_q, d_ff_6_qn, d_ff_7_q, d_ff_7_qn, d_ff_8_q, d_ff_8_qn, d_ff_9_q, d_ff_9_qn,
       d_ff_10_q, d_ff_10_qn, d_ff_11_q, d_ff_11_qn, d_ff_12_q, d_ff_12_qn, d_ff_13_q, d_ff_13_qn, d_ff_14_q,
       d_ff_14_qn, d_ff_15_q, d_ff_15_qn, d_ff_16_q, d_ff_16_qn, d_ff_17_q, d_ff_17_qn, d_ff_18_q,
       d_ff_18_qn, d_ff_19_q, d_ff_19_qn, d_ff_20_q, d_ff_20_qn, d_ff_21_q, d_ff_21_qn, d_ff_22_q,
       d_ff_22_qn, d_ff_23_q, d_ff_23_qn, d_ff_24_q, d_ff_24_qn, d_ff_25_q, d_ff_25_qn, d_ff_26_q,
       d_ff_26_qn, d_ff_27_q, d_ff_27_qn, d_ff_28_q, d_ff_28_qn, d_ff_29_q, d_ff_29_qn, d_ff_30_q,
       d_ff_30_qn, d_ff_31_q, d_ff_31_qn, d_ff_32_q, d_ff_32_qn, d_ff_33_q, d_ff_33_qn, d_ff_34_q,
       d_ff_34_qn, d_ff_35_q, d_ff_35_qn, d_ff_36_q, d_ff_36_qn, d_ff_37_q, d_ff_37_qn, d_ff_38_q,
       d_ff_38_qn, d_ff_39_q, d_ff_39_qn, d_ff_40_q, d_ff_40_qn, d_ff_41_q, d_ff_41_qn, d_ff_42_q,
       d_ff_42_qn, d_ff_43_q, d_ff_43_qn, d_ff_44_q, d_ff_44_qn, d_ff_45_q, d_ff_45_qn, d_ff_46_q,
       d_ff_46_qn, d_ff_47_q, d_ff_47_qn, d_ff_48_q, d_ff_48_qn, decoder_1_out0, decoder_1_out1,
       decoder_1_out2, decoder_1_out3, not_1_out, not_2_out, not_3_out, not_4_out, not_5_out;
  wire [1:0] or_2_out;
  wire [11:0] and_10_out, and_11_out, and_12_out, and_13_out;

  Button button_1 (.out(button_1_out));
  LED led_1 (.in(and_4_out));
  not not_1 (not_1_out, and_4_out);
  LED led_2 (.in(not_1_out));
  not not_2 (not_2_out, Candidate__1);
  not not_3 (not_3_out, Candidate__2);
  not not_4 (not_4_out, Candidate__3);
  not not_5 (not_5_out, Candidate__4);
  and and_1 (and_1_out, Candidate__1, not_3_out, not_4_out, not_5_out);
  and and_2 (and_2_out, not_2_out, Candidate__2, not_4_out, not_5_out);
  and and_3 (and_3_out, not_2_out, not_3_out, Candidate__3, not_5_out);
  and and_4 (and_4_out, Criteria__1, Criteria__2, Criteria__3);
  or or_1 (or_2_out[1], and_5_out, and_3_out);
  or or_2 (or_2_out[0], and_5_out, and_2_out);
  and and_5 (and_5_out, not_2_out, not_3_out, not_4_out, Candidate__4);
  Decoder #(.select(2)) decoder_1 (
    .out0(decoder_1_out0), .out1(decoder_1_out1), .out2(decoder_1_out2), .out3(decoder_1_out3),
    .sel(or_2_out), .en(and_4_out));
  Button button_2 (.out(button_2_out));
  Button button_3 (.out(button_3_out));
  and and_6 (and_6_out, decoder_1_out0, and_1_out, button_1_out);
  and and_7 (and_7_out, decoder_1_out1, button_1_out);
  and and_8 (and_8_out, decoder_1_out2, button_1_out);
  and and_9 (and_9_out, button_1_out, decoder_1_out3);
  D_Flip_Flop d_ff_1 (
    .D(d_ff_1_qn), .clk(and_6_out), .Q(d_ff_1_q), .Qn(d_ff_1_qn), .reset(button_3_out));  // open: preset
  D_Flip_Flop d_ff_2 (
    .D(d_ff_2_qn), .clk(and_7_out), .Q(d_ff_2_q), .Qn(d_ff_2_qn), .reset(button_3_out));  // open: preset
  D_Flip_Flop d_ff_3 (
    .D(d_ff_3_qn), .clk(and_8_out), .Q(d_ff_3_q), .Qn(d_ff_3_qn), .reset(button_3_out));  // open: preset
  D_Flip_Flop d_ff_4 (
    .D(d_ff_4_qn), .clk(and_9_out), .Q(d_ff_4_q), .Qn(d_ff_4_qn), .reset(button_3_out));  // open: preset
  and and_10 (and_10_out[0], button_2_out, d_ff_1_q);
  D_Flip_Flop d_ff_5 (
    .D(d_ff_5_qn), .clk(d_ff_1_qn), .Q(d_ff_5_q), .Qn(d_ff_5_qn), .reset(button_3_out));  // open: preset
  and and_11 (and_11_out[0], button_2_out, d_ff_2_q);
  D_Flip_Flop d_ff_6 (
    .D(d_ff_6_qn), .clk(d_ff_2_qn), .Q(d_ff_6_q), .Qn(d_ff_6_qn), .reset(button_3_out));  // open: preset
  and and_12 (and_12_out[0], button_2_out, d_ff_3_q);
  D_Flip_Flop d_ff_7 (
    .D(d_ff_7_qn), .clk(d_ff_3_qn), .Q(d_ff_7_q), .Qn(d_ff_7_qn), .reset(button_3_out));  // open: preset
  and and_13 (and_13_out[0], button_2_out, d_ff_4_q);
  D_Flip_Flop d_ff_8 (
    .D(d_ff_8_qn), .clk(d_ff_4_qn), .Q(d_ff_8_q), .Qn(d_ff_8_qn), .reset(button_3_out));  // open: preset
  and and_14 (and_10_out[1], button_2_out, d_ff_5_q);
  D_Flip_Flop d_ff_9 (
    .D(d_ff_9_qn), .clk(d_ff_5_qn), .Q(d_ff_9_q), .Qn(d_ff_9_qn), .reset(button_3_out));  // open: preset
  and and_15 (and_11_out[1], button_2_out, d_ff_6_q);
  D_Flip_Flop d_ff_10 (
    .D(d_ff_10_qn), .clk(d_ff_6_qn), .Q(d_ff_10_q), .Qn(d_ff_10_qn), .reset(button_3_out));  // open: preset
  and and_16 (and_12_out[1], button_2_out, d_ff_7_q);
  D_Flip_Flop d_ff_11 (
    .D(d_ff_11_qn), .clk(d_ff_7_qn), .Q(d_ff_11_q), .Qn(d_ff_11_qn), .reset(button_3_out));  // open: preset
  and and_17 (and_13_out[1], button_2_out, d_ff_8_q);
  D_Flip_Flop d_ff_12 (
    .D(d_ff_12_qn), .clk(d_ff_8_qn), .Q(d_ff_12_q), .Qn(d_ff_12_qn), .reset(button_3_out));  // open: preset
  and and_18 (and_10_out[2], button_2_out, d_ff_9_q);
  D_Flip_Flop d_ff_13 (
    .D(d_ff_13_qn), .clk(d_ff_9_qn), .Q(d_ff_13_q), .Qn(d_ff_13_qn), .reset(button_3_out));  // open: preset
  and and_19 (and_11_out[2], button_2_out, d_ff_10_q);
  D_Flip_Flop d_ff_14 (
    .D(d_ff_14_qn), .clk(d_ff_10_qn), .Q(d_ff_14_q), .Qn(d_ff_14_qn), .reset(button_3_out));  // open: preset
  and and_20 (and_12_out[2], button_2_out, d_ff_11_q);
  D_Flip_Flop d_ff_15 (
    .D(d_ff_15_qn), .clk(d_ff_11_qn), .Q(d_ff_15_q), .Qn(d_ff_15_qn), .reset(button_3_out));  // open: preset
  and and_21 (and_13_out[2], button_2_out, d_ff_12_q);
  D_Flip_Flop d_ff_16 (
    .D(d_ff_16_qn), .clk(d_ff_12_qn), .Q(d_ff_16_q), .Qn(d_ff_16_qn), .reset(button_3_out));  // open: preset
  and and_22 (and_10_out[3], button_2_out, d_ff_13_q);
  D_Flip_Flop d_ff_17 (
    .D(d_ff_17_qn), .clk(d_ff_13_qn), .Q(d_ff_17_q), .Qn(d_ff_17_qn), .reset(button_3_out));  // open: preset
  and and_23 (and_11_out[3], button_2_out, d_ff_14_q);
  D_Flip_Flop d_ff_18 (
    .D(d_ff_18_qn), .clk(d_ff_14_qn), .Q(d_ff_18_q), .Qn(d_ff_18_qn), .reset(button_3_out));  // open: preset
  and and_24 (and_12_out[3], button_2_out, d_ff_15_q);
  D_Flip_Flop d_ff_19 (
    .D(d_ff_19_qn), .clk(d_ff_15_qn), .Q(d_ff_19_q), .Qn(d_ff_19_qn), .reset(button_3_out));  // open: preset
  and and_25 (and_13_out[3], button_2_out, d_ff_16_q);
  D_Flip_Flop d_ff_20 (
    .D(d_ff_20_qn), .clk(d_ff_16_qn), .Q(d_ff_20_q), .Qn(d_ff_20_qn), .reset(button_3_out));  // open: preset
  D_Flip_Flop d_ff_21 (
    .D(d_ff_21_qn), .clk(d_ff_17_qn), .Q(d_ff_21_q), .Qn(d_ff_21_qn), .reset(button_3_out));  // open: preset
  D_Flip_Flop d_ff_22 (
    .D(d_ff_22_qn), .clk(d_ff_18_qn), .Q(d_ff_22_q), .Qn(d_ff_22_qn), .reset(button_3_out));  // open: preset
  and and_26 (and_10_out[4], button_2_out, d_ff_17_q);
  and and_27 (and_11_out[4], button_2_out, d_ff_18_q);
  and and_28 (and_12_out[4], button_2_out, d_ff_19_q);
  D_Flip_Flop d_ff_23 (
    .D(d_ff_23_qn), .clk(d_ff_19_qn), .Q(d_ff_23_q), .Qn(d_ff_23_qn), .reset(button_3_out));  // open: preset
  and and_29 (and_13_out[4], button_2_out, d_ff_20_q);
  D_Flip_Flop d_ff_24 (
    .D(d_ff_24_qn), .clk(d_ff_20_qn), .Q(d_ff_24_q), .Qn(d_ff_24_qn), .reset(button_3_out));  // open: preset
  and and_30 (and_10_out[5], button_2_out, d_ff_21_q);
  D_Flip_Flop d_ff_25 (
    .D(d_ff_25_qn), .clk(d_ff_21_qn), .Q(d_ff_25_q), .Qn(d_ff_25_qn), .reset(button_3_out));  // open: preset
  and and_31 (and_11_out[5], button_2_out, d_ff_22_q);
  D_Flip_Flop d_ff_26 (
    .D(d_ff_26_qn), .clk(d_ff_22_qn), .Q(d_ff_26_q), .Qn(d_ff_26_qn), .reset(button_3_out));  // open: preset
  and and_32 (and_12_out[5], button_2_out, d_ff_23_q);
  D_Flip_Flop d_ff_27 (
    .D(d_ff_27_qn), .clk(d_ff_23_qn), .Q(d_ff_27_q), .Qn(d_ff_27_qn), .reset(button_3_out));  // open: preset
  and and_33 (and_13_out[5], button_2_out, d_ff_24_q);
  D_Flip_Flop d_ff_28 (
    .D(d_ff_28_qn), .clk(d_ff_24_qn), .Q(d_ff_28_q), .Qn(d_ff_28_qn), .reset(button_3_out));  // open: preset
  and and_34 (and_10_out[6], button_2_out, d_ff_25_q);
  D_Flip_Flop d_ff_29 (
    .D(d_ff_29_qn), .clk(d_ff_25_qn), .Q(d_ff_29_q), .Qn(d_ff_29_qn), .reset(button_3_out));  // open: preset
  and and_35 (and_11_out[6], button_2_out, d_ff_26_q);
  D_Flip_Flop d_ff_30 (
    .D(d_ff_30_qn), .clk(d_ff_26_qn), .Q(d_ff_30_q), .Qn(d_ff_30_qn), .reset(button_3_out));  // open: preset
  and and_36 (and_12_out[6], button_2_out, d_ff_27_q);
  D_Flip_Flop d_ff_31 (
    .D(d_ff_31_qn), .clk(d_ff_27_qn), .Q(d_ff_31_q), .Qn(d_ff_31_qn), .reset(button_3_out));  // open: preset
  and and_37 (and_13_out[6], button_2_out, d_ff_28_q);
  D_Flip_Flop d_ff_32 (
    .D(d_ff_32_qn), .clk(d_ff_28_qn), .Q(d_ff_32_q), .Qn(d_ff_32_qn), .reset(button_3_out));  // open: preset
  and and_38 (and_10_out[7], button_2_out, d_ff_29_q);
  D_Flip_Flop d_ff_33 (
    .D(d_ff_33_qn), .clk(d_ff_29_qn), .Q(d_ff_33_q), .Qn(d_ff_33_qn), .reset(button_3_out));  // open: preset
  and and_39 (and_11_out[7], button_2_out, d_ff_30_q);
  D_Flip_Flop d_ff_34 (
    .D(d_ff_34_qn), .clk(d_ff_30_qn), .Q(d_ff_34_q), .Qn(d_ff_34_qn), .reset(button_3_out));  // open: preset
  and and_40 (and_12_out[7], button_2_out, d_ff_31_q);
  D_Flip_Flop d_ff_35 (
    .D(d_ff_35_qn), .clk(d_ff_31_qn), .Q(d_ff_35_q), .Qn(d_ff_35_qn), .reset(button_3_out));  // open: preset
  and and_41 (and_13_out[7], button_2_out, d_ff_32_q);
  D_Flip_Flop d_ff_36 (
    .D(d_ff_36_qn), .clk(d_ff_32_qn), .Q(d_ff_36_q), .Qn(d_ff_36_qn), .reset(button_3_out));  // open: preset
  and and_42 (and_10_out[8], button_2_out, d_ff_33_q);
  D_Flip_Flop d_ff_37 (
    .D(d_ff_37_qn), .clk(d_ff_33_qn), .Q(d_ff_37_q), .Qn(d_ff_37_qn), .reset(button_3_out));  // open: preset
  and and_43 (and_11_out[8], button_2_out, d_ff_34_q);
  D_Flip_Flop d_ff_38 (
    .D(d_ff_38_qn), .clk(d_ff_34_qn), .Q(d_ff_38_q), .Qn(d_ff_38_qn), .reset(button_3_out));  // open: preset
  and and_44 (and_12_out[8], button_2_out, d_ff_35_q);
  D_Flip_Flop d_ff_39 (
    .D(d_ff_39_qn), .clk(d_ff_35_qn), .Q(d_ff_39_q), .Qn(d_ff_39_qn), .reset(button_3_out));  // open: preset
  and and_45 (and_13_out[8], button_2_out, d_ff_36_q);
  D_Flip_Flop d_ff_40 (
    .D(d_ff_40_qn), .clk(d_ff_36_qn), .Q(d_ff_40_q), .Qn(d_ff_40_qn), .reset(button_3_out));  // open: preset
  and and_46 (and_10_out[9], button_2_out, d_ff_37_q);
  D_Flip_Flop d_ff_41 (
    .D(d_ff_41_qn), .clk(d_ff_37_qn), .Q(d_ff_41_q), .Qn(d_ff_41_qn), .reset(button_3_out));  // open: preset
  and and_47 (and_11_out[9], button_2_out, d_ff_38_q);
  D_Flip_Flop d_ff_42 (
    .D(d_ff_42_qn), .clk(d_ff_38_qn), .Q(d_ff_42_q), .Qn(d_ff_42_qn), .reset(button_3_out));  // open: preset
  D_Flip_Flop d_ff_43 (
    .D(d_ff_43_qn), .clk(d_ff_39_qn), .Q(d_ff_43_q), .Qn(d_ff_43_qn), .reset(button_3_out));  // open: preset
  D_Flip_Flop d_ff_44 (
    .D(d_ff_44_qn), .clk(d_ff_40_qn), .Q(d_ff_44_q), .Qn(d_ff_44_qn), .reset(button_3_out));  // open: preset
  D_Flip_Flop d_ff_45 (
    .D(d_ff_45_qn), .clk(d_ff_41_qn), .Q(d_ff_45_q), .Qn(d_ff_45_qn), .reset(button_3_out));  // open: preset
  D_Flip_Flop d_ff_46 (
    .D(d_ff_46_qn), .clk(d_ff_42_qn), .Q(d_ff_46_q), .Qn(d_ff_46_qn), .reset(button_3_out));  // open: preset
  and and_48 (and_12_out[9], button_2_out, d_ff_39_q);
  and and_49 (and_13_out[9], button_2_out, d_ff_40_q);
  and and_50 (and_10_out[10], button_2_out, d_ff_41_q);
  and and_51 (and_11_out[10], button_2_out, d_ff_42_q);
  and and_52 (and_12_out[10], button_2_out, d_ff_43_q);
  D_Flip_Flop d_ff_47 (
    .D(d_ff_47_qn), .clk(d_ff_43_qn), .Q(d_ff_47_q), .Qn(d_ff_47_qn), .reset(button_3_out));  // open: preset
  and and_53 (and_13_out[10], button_2_out, d_ff_44_q);
  D_Flip_Flop d_ff_48 (
    .D(d_ff_48_qn), .clk(d_ff_44_qn), .Q(d_ff_48_q), .Qn(d_ff_48_qn), .reset(button_3_out));  // open: preset
  and and_54 (and_10_out[11], button_2_out, d_ff_45_q);
  and and_55 (and_11_out[11], button_2_out, d_ff_46_q);
  and and_56 (and_12_out[11], button_2_out, d_ff_47_q);
  and and_57 (and_13_out[11], button_2_out, d_ff_48_q);
  // Binary_to_BCD_converter #(.binvalue(12)) binary_to_bcd_converter_1: pin names not known; wires that end beside it: and_10_out, binary_to_bcd_converter_1_p2, binary_to_bcd_converter_1_p3, binary_to_bcd_converter_1_p4, binary_to_bcd_converter_1_p5
  // Binary_to_BCD_converter #(.binvalue(12)) binary_to_bcd_converter_2: pin names not known; wires that end beside it: and_11_out, binary_to_bcd_converter_2_p2, binary_to_bcd_converter_2_p3, binary_to_bcd_converter_2_p4, binary_to_bcd_converter_2_p5
  // Binary_to_BCD_converter #(.binvalue(12)) binary_to_bcd_converter_3: pin names not known; wires that end beside it: and_12_out, binary_to_bcd_converter_3_p2, binary_to_bcd_converter_3_p3, binary_to_bcd_converter_3_p4, binary_to_bcd_converter_3_p5
  // Binary_to_BCD_converter #(.binvalue(12)) binary_to_bcd_converter_4: pin names not known; wires that end beside it: and_13_out, binary_to_bcd_converter_4_p2, binary_to_bcd_converter_4_p3, binary_to_bcd_converter_4_p4, binary_to_bcd_converter_4_p5
  _7_Segment_Display u_7_segment_display_1 (
    .g(bcd_to_7_segment_decoder_1_p1), .f(bcd_to_7_segment_decoder_1_p3), .a(bcd_to_7_segment_decoder_1_p6),
    .b(bcd_to_7_segment_decoder_1_p8), .e(bcd_to_7_segment_decoder_1_p2), .d(bcd_to_7_segment_decoder_1_p4),
    .c(bcd_to_7_segment_decoder_1_p7));  // open: dp
  // BCD_to_7_Segment_decoder bcd_to_7_segment_decoder_1: pin names not known; wires that end beside it: bcd_to_7_segment_decoder_1_p1, bcd_to_7_segment_decoder_1_p2, bcd_to_7_segment_decoder_1_p3, bcd_to_7_segment_decoder_1_p4, binary_to_bcd_converter_1_p2, bcd_to_7_segment_decoder_1_p6, bcd_to_7_segment_decoder_1_p7, bcd_to_7_segment_decoder_1_p8
  _7_Segment_Display u_7_segment_display_2 (
    .g(bcd_to_7_segment_decoder_2_p1), .f(bcd_to_7_segment_decoder_2_p3), .a(bcd_to_7_segment_decoder_2_p6),
    .b(bcd_to_7_segment_decoder_2_p8), .e(bcd_to_7_segment_decoder_2_p2), .d(bcd_to_7_segment_decoder_2_p4),
    .c(bcd_to_7_segment_decoder_2_p7));  // open: dp
  // BCD_to_7_Segment_decoder bcd_to_7_segment_decoder_2: pin names not known; wires that end beside it: bcd_to_7_segment_decoder_2_p1, bcd_to_7_segment_decoder_2_p2, bcd_to_7_segment_decoder_2_p3, bcd_to_7_segment_decoder_2_p4, binary_to_bcd_converter_2_p2, bcd_to_7_segment_decoder_2_p6, bcd_to_7_segment_decoder_2_p7, bcd_to_7_segment_decoder_2_p8
  _7_Segment_Display u_7_segment_display_3 (
    .g(bcd_to_7_segment_decoder_3_p1), .f(bcd_to_7_segment_decoder_3_p3), .a(bcd_to_7_segment_decoder_3_p6),
    .b(bcd_to_7_segment_decoder_3_p8), .e(bcd_to_7_segment_decoder_3_p2), .d(bcd_to_7_segment_decoder_3_p4),
    .c(bcd_to_7_segment_decoder_3_p7));  // open: dp
  // BCD_to_7_Segment_decoder bcd_to_7_segment_decoder_3: pin names not known; wires that end beside it: bcd_to_7_segment_decoder_3_p1, bcd_to_7_segment_decoder_3_p2, bcd_to_7_segment_decoder_3_p3, bcd_to_7_segment_decoder_3_p4, binary_to_bcd_converter_3_p2, bcd_to_7_segment_decoder_3_p6, bcd_to_7_segment_decoder_3_p7, bcd_to_7_segment_decoder_3_p8
  _7_Segment_Display u_7_segment_display_4 (
    .g(bcd_to_7_segment_decoder_4_p1), .f(bcd_to_7_segment_decoder_4_p3), .a(bcd_to_7_segment_decoder_4_p6),
    .b(bcd_to_7_segment_decoder_4_p8), .e(bcd_to_7_segment_decoder_4_p2), .d(bcd_to_7_segment_decoder_4_p4),
    .c(bcd_to_7_segment_decoder_4_p7));  // open: dp
  // BCD_to_7_Segment_decoder bcd_to_7_segment_decoder_4: pin names not known; wires that end beside it: bcd_to_7_segment_decoder_4_p1, bcd_to_7_segment_decoder_4_p2, bcd_to_7_segment_decoder_4_p3, bcd_to_7_segment_decoder_4_p4, binary_to_bcd_converter_4_p2, bcd_to_7_segment_decoder_4_p6, bcd_to_7_segment_decoder_4_p7, bcd_to_7_segment_decoder_4_p8
  _7_Segment_Display u_7_segment_display_5 (
    .g(bcd_to_7_segment_decoder_5_p1), .f(bcd_to_7_segment_decoder_5_p3), .a(bcd_to_7_segment_decoder_5_p6),
    .b(bcd_to_7_segment_decoder_5_p8), .e(bcd_to_7_segment_decoder_5_p2), .d(bcd_to_7_segment_decoder_5_p4),
    .c(bcd_to_7_segment_decoder_5_p7));  // open: dp
  // BCD_to_7_Segment_decoder bcd_to_7_segment_decoder_5: pin names not known; wires that end beside it: bcd_to_7_segment_decoder_5_p1, bcd_to_7_segment_decoder_5_p2, bcd_to_7_segment_decoder_5_p3, bcd_to_7_segment_decoder_5_p4, binary_to_bcd_converter_1_p3, bcd_to_7_segment_decoder_5_p6, bcd_to_7_segment_decoder_5_p7, bcd_to_7_segment_decoder_5_p8
  _7_Segment_Display u_7_segment_display_6 (
    .g(bcd_to_7_segment_decoder_6_p1), .f(bcd_to_7_segment_decoder_6_p3), .a(bcd_to_7_segment_decoder_6_p6),
    .b(bcd_to_7_segment_decoder_6_p8), .e(bcd_to_7_segment_decoder_6_p2), .d(bcd_to_7_segment_decoder_6_p4),
    .c(bcd_to_7_segment_decoder_6_p7));  // open: dp
  // BCD_to_7_Segment_decoder bcd_to_7_segment_decoder_6: pin names not known; wires that end beside it: bcd_to_7_segment_decoder_6_p1, bcd_to_7_segment_decoder_6_p2, bcd_to_7_segment_decoder_6_p3, bcd_to_7_segment_decoder_6_p4, binary_to_bcd_converter_2_p3, bcd_to_7_segment_decoder_6_p6, bcd_to_7_segment_decoder_6_p7, bcd_to_7_segment_decoder_6_p8
  _7_Segment_Display u_7_segment_display_7 (
    .g(bcd_to_7_segment_decoder_7_p1), .f(bcd_to_7_segment_decoder_7_p3), .a(bcd_to_7_segment_decoder_7_p6),
    .b(bcd_to_7_segment_decoder_7_p8), .e(bcd_to_7_segment_decoder_7_p2), .d(bcd_to_7_segment_decoder_7_p4),
    .c(bcd_to_7_segment_decoder_7_p7));  // open: dp
  // BCD_to_7_Segment_decoder bcd_to_7_segment_decoder_7: pin names not known; wires that end beside it: bcd_to_7_segment_decoder_7_p1, bcd_to_7_segment_decoder_7_p2, bcd_to_7_segment_decoder_7_p3, bcd_to_7_segment_decoder_7_p4, binary_to_bcd_converter_3_p3, bcd_to_7_segment_decoder_7_p6, bcd_to_7_segment_decoder_7_p7, bcd_to_7_segment_decoder_7_p8
  _7_Segment_Display u_7_segment_display_8 (
    .g(bcd_to_7_segment_decoder_8_p1), .f(bcd_to_7_segment_decoder_8_p3), .a(bcd_to_7_segment_decoder_8_p6),
    .b(bcd_to_7_segment_decoder_8_p8), .e(bcd_to_7_segment_decoder_8_p2), .d(bcd_to_7_segment_decoder_8_p4),
    .c(bcd_to_7_segment_decoder_8_p7));  // open: dp
  // BCD_to_7_Segment_decoder bcd_to_7_segment_decoder_8: pin names not known; wires that end beside it: bcd_to_7_segment_decoder_8_p1, bcd_to_7_segment_decoder_8_p2, bcd_to_7_segment_decoder_8_p3, bcd_to_7_segment_decoder_8_p4, binary_to_bcd_converter_4_p3, bcd_to_7_segment_decoder_8_p6, bcd_to_7_segment_decoder_8_p7, bcd_to_7_segment_decoder_8_p8
  _7_Segment_Display u_7_segment_display_9 (
    .g(bcd_to_7_segment_decoder_9_p1), .f(bcd_to_7_segment_decoder_9_p3), .a(bcd_to_7_segment_decoder_9_p6),
    .b(bcd_to_7_segment_decoder_9_p8), .e(bcd_to_7_segment_decoder_9_p2), .d(bcd_to_7_segment_decoder_9_p4),
    .c(bcd_to_7_segment_decoder_9_p7));  // open: dp
  // BCD_to_7_Segment_decoder bcd_to_7_segment_decoder_9: pin names not known; wires that end beside it: bcd_to_7_segment_decoder_9_p1, bcd_to_7_segment_decoder_9_p2, bcd_to_7_segment_decoder_9_p3, bcd_to_7_segment_decoder_9_p4, binary_to_bcd_converter_1_p4, bcd_to_7_segment_decoder_9_p6, bcd_to_7_segment_decoder_9_p7, bcd_to_7_segment_decoder_9_p8
  _7_Segment_Display u_7_segment_display_10 (
    .g(bcd_to_7_segment_decoder_10_p1), .f(bcd_to_7_segment_decoder_10_p3),
    .a(bcd_to_7_segment_decoder_10_p6), .b(bcd_to_7_segment_decoder_10_p8),
    .e(bcd_to_7_segment_decoder_10_p2), .d(bcd_to_7_segment_decoder_10_p4), .c(bcd_to_7_segment_decoder_10_p7));  // open: dp
  // BCD_to_7_Segment_decoder bcd_to_7_segment_decoder_10: pin names not known; wires that end beside it: bcd_to_7_segment_decoder_10_p1, bcd_to_7_segment_decoder_10_p2, bcd_to_7_segment_decoder_10_p3, bcd_to_7_segment_decoder_10_p4, binary_to_bcd_converter_2_p4, bcd_to_7_segment_decoder_10_p6, bcd_to_7_segment_decoder_10_p7, bcd_to_7_segment_decoder_10_p8
  _7_Segment_Display u_7_segment_display_11 (
    .g(bcd_to_7_segment_decoder_11_p1), .f(bcd_to_7_segment_decoder_11_p3),
    .a(bcd_to_7_segment_decoder_11_p6), .b(bcd_to_7_segment_decoder_11_p8),
    .e(bcd_to_7_segment_decoder_11_p2), .d(bcd_to_7_segment_decoder_11_p4), .c(bcd_to_7_segment_decoder_11_p7));  // open: dp
  // BCD_to_7_Segment_decoder bcd_to_7_segment_decoder_11: pin names not known; wires that end beside it: bcd_to_7_segment_decoder_11_p1, bcd_to_7_segment_decoder_11_p2, bcd_to_7_segment_decoder_11_p3, bcd_to_7_segment_decoder_11_p4, binary_to_bcd_converter_3_p4, bcd_to_7_segment_decoder_11_p6, bcd_to_7_segment_decoder_11_p7, bcd_to_7_segment_decoder_11_p8
  _7_Segment_Display u_7_segment_display_12 (
    .g(bcd_to_7_segment_decoder_12_p1), .f(bcd_to_7_segment_decoder_12_p3),
    .a(bcd_to_7_segment_decoder_12_p6), .b(bcd_to_7_segment_decoder_12_p8),
    .e(bcd_to_7_segment_decoder_12_p2), .d(bcd_to_7_segment_decoder_12_p4), .c(bcd_to_7_segment_decoder_12_p7));  // open: dp
  // BCD_to_7_Segment_decoder bcd_to_7_segment_decoder_12: pin names not known; wires that end beside it: bcd_to_7_segment_decoder_12_p1, bcd_to_7_segment_decoder_12_p2, bcd_to_7_segment_decoder_12_p3, bcd_to_7_segment_decoder_12_p4, binary_to_bcd_converter_4_p4, bcd_to_7_segment_decoder_12_p6, bcd_to_7_segment_decoder_12_p7, bcd_to_7_segment_decoder_12_p8
  _7_Segment_Display u_7_segment_display_13 (
    .g(bcd_to_7_segment_decoder_13_p1), .f(bcd_to_7_segment_decoder_13_p3),
    .a(bcd_to_7_segment_decoder_13_p6), .b(bcd_to_7_segment_decoder_13_p8),
    .e(bcd_to_7_segment_decoder_13_p2), .d(bcd_to_7_segment_decoder_13_p4), .c(bcd_to_7_segment_decoder_13_p7));  // open: dp
  // BCD_to_7_Segment_decoder bcd_to_7_segment_decoder_13: pin names not known; wires that end beside it: bcd_to_7_segment_decoder_13_p1, bcd_to_7_segment_decoder_13_p2, bcd_to_7_segment_decoder_13_p3, bcd_to_7_segment_decoder_13_p4, binary_to_bcd_converter_1_p5, bcd_to_7_segment_decoder_13_p6, bcd_to_7_segment_decoder_13_p7, bcd_to_7_segment_decoder_13_p8
  _7_Segment_Display u_7_segment_display_14 (
    .g(bcd_to_7_segment_decoder_14_p1), .f(bcd_to_7_segment_decoder_14_p3),
    .a(bcd_to_7_segment_decoder_14_p6), .b(bcd_to_7_segment_decoder_14_p8),
    .e(bcd_to_7_segment_decoder_14_p2), .d(bcd_to_7_segment_decoder_14_p4), .c(bcd_to_7_segment_decoder_14_p7));  // open: dp
  // BCD_to_7_Segment_decoder bcd_to_7_segment_decoder_14: pin names not known; wires that end beside it: bcd_to_7_segment_decoder_14_p1, bcd_to_7_segment_decoder_14_p2, bcd_to_7_segment_decoder_14_p3, bcd_to_7_segment_decoder_14_p4, binary_to_bcd_converter_2_p5, bcd_to_7_segment_decoder_14_p6, bcd_to_7_segment_decoder_14_p7, bcd_to_7_segment_decoder_14_p8
  _7_Segment_Display u_7_segment_display_15 (
    .g(bcd_to_7_segment_decoder_15_p1), .f(bcd_to_7_segment_decoder_15_p3),
    .a(bcd_to_7_segment_decoder_15_p6), .b(bcd_to_7_segment_decoder_15_p8),
    .e(bcd_to_7_segment_decoder_15_p2), .d(bcd_to_7_segment_decoder_15_p4), .c(bcd_to_7_segment_decoder_15_p7));  // open: dp
  // BCD_to_7_Segment_decoder bcd_to_7_segment_decoder_15: pin names not known; wires that end beside it: bcd_to_7_segment_decoder_15_p1, bcd_to_7_segment_decoder_15_p2, bcd_to_7_segment_decoder_15_p3, bcd_to_7_segment_decoder_15_p4, binary_to_bcd_converter_3_p5, bcd_to_7_segment_decoder_15_p6, bcd_to_7_segment_decoder_15_p7, bcd_to_7_segment_decoder_15_p8
  _7_Segment_Display u_7_segment_display_16 (
    .g(bcd_to_7_segment_decoder_16_p1), .f(bcd_to_7_segment_decoder_16_p3),
    .a(bcd_to_7_segment_decoder_16_p6), .b(bcd_to_7_segment_decoder_16_p8),
    .e(bcd_to_7_segment_decoder_16_p2), .d(bcd_to_7_segment_decoder_16_p4), .c(bcd_to_7_segment_decoder_16_p7));  // open: dp
  // BCD_to_7_Segment_decoder bcd_to_7_segment_decoder_16: pin names not known; wires that end beside it: bcd_to_7_segment_decoder_16_p1, bcd_to_7_segment_decoder_16_p2, bcd_to_7_segment_decoder_16_p3, bcd_to_7_segment_decoder_16_p4, binary_to_bcd_converter_4_p5, bcd_to_7_segment_decoder_16_p6, bcd_to_7_segment_decoder_16_p7, bcd_to_7_segment_decoder_16_p8

  // Notes on the sheet:
  //   NOT ELIGIBLE TO VOTE
  //   Select Candidates:
  //   Confirm VOTE
  //   ELIGIBLE TO VOTE
  //   Eligibility To Vote:
  //   View All Candidate Votes
  //   Reset All Votes
  //   VOTE COUNT: CANDIDATE 1
  //   VOTE COUNT: CANDIDATE 2
  //   VOTE COUNT: CANDIDATE 3
  //   VOTE COUNT: CANDIDATE 4
endmodule
